# Fritzing sketch Monster-in-a-box (saved by Fritzing 0.9.3b)

parts:
  Raspberry_Pi_1 = Raspberry Pi 3 [part_number=RPI-3-V1.2]
  U2 = 4-Channel 5v Relay Shield [package=relay-4ch5v10a]
  L2 = Solenoid
  SPKR1 = Loudspeaker  # not connected
  L1 = Solenoid
  VCC1 = Battery
  S2 = SWITCH-MOMENTARY-2 [package=tactile-pth-12mm]

nets:
  N1: Raspberry_Pi_1.GIPO23, U2.IN4
  N2: Raspberry_Pi_1.GIPO18, U2.IN3
  N3: Raspberry_Pi_1.GIPO15, U2.IN2
  N4: Raspberry_Pi_1.GIPO14, U2.IN1
  GND: Raspberry_Pi_1.GND, U2.GND
  5V: Raspberry_Pi_1.5V, U2.VCC
  N5: U2.K1-Off, U2.K2-Off, VCC1.+
  N6: U2.K1-On, L1.pin2
  N7: U2.K2-On, L2.pin2
  N8: U2.K3-Off, S2.2
  N9: U2.K3-On, S2.1

notes:
  Door Lock Actuator 1
  Fog Machine Momentary button
  4 Channel Relay
  RaspberryPi 3
  Door Lock Actuator 2
  Powered Speaker
  5v connected to VCC
  GND connected to GND
  GPIO14 connected to IN1
  GPIO15 connected to IN2
  GPIO18 connected to IN3
  GPIO23 connected to IN4
  Computer Power Supply (12vdc / 5vdc)
  12vdc

custom parts:
  4-Channel 5v Relay Shield: 4 Channel 5v Relay Shield w. 2x SPD-06VDC-SD-C
